# Fritzing sketch fritzing2 (saved by Fritzing 0.9.5d)

parts:
  Nau7802 = Adafruit NAU7802
  Part2 = Adafruit NAU7802
  Part3 = Adafruit DRV8833 DC/Stepper Motor Driver [part_number="Adafruit #3297"]
  U1 = Vibration Motor- ROB-08449 [package=vibe-motor-10mm]
  U2 = mini DIN 5 Connector [package=mini-din5]
  JP1 = BF350-3EB [package=screwterminal-3.5mm-4_lock]
  JP2 = BF350-3EB [package=screwterminal-3.5mm-4_lock]
  Mod1 = Raspberry Pi Pico
  buzzer = Piezo Speaker

nets (from the breadboard view):
  GND: Nau7802.GND, Part3.GND, JP1.3, buzzer.pin1
  VCC: Nau7802.VCC, Part2.VCC, Part3.VMOTOR, U2.1, Mod1.pin_36
  N1: Nau7802.SCL, Mod1.pin_7
  N2: Nau7802.SDA, Mod1.pin_6
  N3: Nau7802.A+, JP1.2
  N4: Nau7802.A-, JP1.4
  N5: Nau7802.AVDD, JP1.1
  N6: Part2.GND, U2.5, JP2.3, Mod1.pin_3, Mod1.pin_38
  N7: Part2.SCL, Mod1.pin_20
  N8: Part2.SDA, Mod1.pin_19
  N9: Part2.A+, JP2.2
  N10: Part2.A-, JP2.4
  N11: Part2.AVDD, JP2.1
  N12: Part3.AOUT2, U1.-
  N13: Part3.AOUT1, U1.+
  N14: Part3.!SLEEP, Mod1.pin_31
  N15: Part3.AIN2, Mod1.pin_34
  N16: Part3.AIN1, Mod1.pin_32
  N17: U2.2, Mod1.pin_2
  N18: U2.3, Mod1.pin_4
  N19: U2.4, Mod1.pin_1
  N20: Mod1.pin_9, buzzer.pin2

custom parts:
  Adafruit DRV8833 DC/Stepper Motor Driver: Spin two DC motors or step one bi-polar or uni-polar stepper with up to 1.2A per channel using the DRV8833. This motor driver chip is a nice alternative to the TB6612 driver. Like that chip, you get 2 full H-bridges, but this chip is better for low voltage uses (can run from 2.7V up to 10.8V motor power) and has built in current limiting capability. We set it up for 1A current limiting so you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
  BF350-3EB: Full bridge 350oms strain gauge
  Raspberry Pi Pico: Raspberry Pi Pico. Based around the RP2040 microcontroller the Pico is a low cost microcontroller device bringing Raspberry Pi quality, cost, and easy of use to the microcontroller space. Jan 2021, Split part in to two versions: tht (this one) and SMD. This one will drill holes for a .1 in header in pcb to allow plugging in the module as well as providing pads to solder the module to the top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
